// Logisim project 8bit_full-adder.circ as structural Verilog: 2 circuits, main circuit 8BIT_FULL-ADDER
module _1BIT_FULL_ADDER (
  input  Cin,
  input  A,
  input  B,
  output SUM,
  output Cout
);

  wire and_1_out, and_2_out, and_3_out, or_1_out, xor_1_out;

  xor xor_1 (xor_1_out, A, B);
  and and_1 (and_1_out, Cin, A);
  and and_2 (and_2_out, Cin, B);
  xor xor_2 (SUM, Cin, xor_1_out);
  or or_1 (or_1_out, and_1_out, and_2_out);
  and and_3 (and_3_out, A, B);
  or or_2 (Cout, or_1_out, and_3_out);
endmodule

module _8BIT_FULL_ADDER (
  input  Cin,
  input  A1,
  input  B1,
  input  A2,
  input  B2,
  input  A3,
  input  B3,
  input  A4,
  input  B4,
  input  A5,
  input  B5,
  input  A6,
  input  B6,
  input  A7,
  input  B7,
  input  A8,
  input  B8,
  output out_18,
  output out_19,
  output out_20,
  output out_21,
  output out_22,
  output out_23,
  output out_24,
  output out_25,
  output out_26
);

  wire _1BIT_FULL_ADDER_2_cout, _1BIT_FULL_ADDER_3_cout, _1BIT_FULL_ADDER_4_cout, _1BIT_FULL_ADDER_5_cout,
       _1BIT_FULL_ADDER_6_cout, _1BIT_FULL_ADDER_7_cout, _1BIT_FULL_ADDER_cout;

  _1BIT_FULL_ADDER _1BIT_FULL_ADDER (.SUM(out_18), .Cout(_1BIT_FULL_ADDER_cout), .Cin(Cin), .A(A1), .B(B1));
  _1BIT_FULL_ADDER _1BIT_FULL_ADDER_2 (
    .SUM(out_19), .Cout(_1BIT_FULL_ADDER_2_cout), .Cin(_1BIT_FULL_ADDER_cout), .A(A2), .B(B2));
  _1BIT_FULL_ADDER _1BIT_FULL_ADDER_3 (
    .SUM(out_20), .Cout(_1BIT_FULL_ADDER_3_cout), .Cin(_1BIT_FULL_ADDER_2_cout), .A(A3), .B(B3));
  _1BIT_FULL_ADDER _1BIT_FULL_ADDER_4 (
    .SUM(out_21), .Cout(_1BIT_FULL_ADDER_4_cout), .Cin(_1BIT_FULL_ADDER_3_cout), .A(A4), .B(B4));
  _1BIT_FULL_ADDER _1BIT_FULL_ADDER_5 (
    .SUM(out_22), .Cout(_1BIT_FULL_ADDER_5_cout), .Cin(_1BIT_FULL_ADDER_4_cout), .A(A5), .B(B5));
  _1BIT_FULL_ADDER _1BIT_FULL_ADDER_6 (
    .SUM(out_23), .Cout(_1BIT_FULL_ADDER_6_cout), .Cin(_1BIT_FULL_ADDER_5_cout), .A(A6), .B(B6));
  _1BIT_FULL_ADDER _1BIT_FULL_ADDER_7 (
    .SUM(out_24), .Cout(_1BIT_FULL_ADDER_7_cout), .Cin(_1BIT_FULL_ADDER_6_cout), .A(A7), .B(B7));
  _1BIT_FULL_ADDER _1BIT_FULL_ADDER_8 (.SUM(out_25), .Cout(out_26), .Cin(_1BIT_FULL_ADDER_7_cout), .A(A8), .B(B8));
endmodule
